// Logisim project alu.circ as structural Verilog: 13 circuits, main circuit main
module main (
  input  [2:0] op_code,
  input  [7:0] x,
  input  [7:0] y,
  output [7:0] result,
  output SF,
  output ZF,
  output CF,
  output OF,
  output EQ
);

  Multiplexer multiplexer_1 (
    .X(x), .Y(y), .op_code(op_code), .SF(SF), .ZF(ZF), .CF(CF), .OF(OF), .EQ(EQ), .result(result));

  // Notes on the sheet:
  //   cs31 lab3, part 2: ALU
  //   Michael Lu, Caroline Yao
  //   Build your ALU here.
endmodule

module Multiplexer (
  input  [2:0] op_code,
  input  [7:0] X,
  input  [7:0] Y,
  output [7:0] result,
  output SF,
  output ZF,
  output CF,
  output OF,
  output EQ
);

  wire add_carry_out, comparator_eq, subtract_carry_out;
  wire [7:0] add_result, arithmetic_shift_right_result, bitwise_and_result, bitwise_or_result,
       comparator_result, left_shift_result, logical_shift_right_result, subtract_result;

  Output_Flag output_flag_1 (
    .Result(result), .OP_Code(op_code), .Add_C_out(add_carry_out), .Sub_C_out(subtract_carry_out), .x(X),
    .EQ_In(comparator_eq), .y(Y), .SF_Out(SF), .ZF_Out(ZF), .CF_Out(CF), .OF(OF), .EQ_Out(EQ));
  Adder add (.X(X), .Y(Y), .Carry_out(add_carry_out), .result(add_result));
  Subtractor subtract (.X(X), .Y(Y), .Carry_out(subtract_carry_out), .result(subtract_result));
  ShiftLeft left_shift (.X(X), .Y(Y), .result(left_shift_result));
  LogicalRightShift logical_shift_right (.X(X), .Y(Y), .result(logical_shift_right_result));
  ArithmeticRightShift arithmetic_shift_right (.X(X), .Y(Y), .result(arithmetic_shift_right_result));
  Comparator comparator (.X(X), .Y(Y), .eq(comparator_eq), .result(comparator_result));
  OrGate bitwise_or (.X(X), .Y(Y), .result(bitwise_or_result));
  AndGate bitwise_and (.X(X), .Y(Y), .result(bitwise_and_result));
  Multiplexer_part #(.select(3), .width(8), .enable("false")) multiplexer_1 (
    .in0(bitwise_or_result), .in1(bitwise_and_result), .in2(add_result), .in3(subtract_result),
    .in4(left_shift_result), .in5(logical_shift_right_result), .in6(arithmetic_shift_right_result),
    .in7(comparator_result), .out(result), .sel(op_code));
endmodule

module OrGate (
  input  [7:0] X,
  input  [7:0] Y,
  output [7:0] result
);

  assign result = X | Y;  // OR_Gate or_1, 8 bits wide
endmodule

module AndGate (
  input  [7:0] X,
  input  [7:0] Y,
  output [7:0] result
);

  assign result = X & Y;  // AND_Gate and_1, 8 bits wide
endmodule

module Adder (
  input  [7:0] X,
  input  [7:0] Y,
  output [7:0] result,
  output Carry_out
);

  Adder_part adder_1 (.a(X), .b(Y), .out(result), .cin(1'b0), .cout(Carry_out));

  // Notes on the sheet:
  //   Carry in
endmodule

module Subtractor (
  input  [7:0] X,
  input  [7:0] Y,
  output [7:0] result,
  output Carry_out
);

  wire [7:0] not_1_out;

  assign not_1_out = ~Y;  // NOT_Gate not_1, 8 bits wide
  Adder_part adder_1 (.a(X), .b(not_1_out), .out(result), .cin(1'b1), .cout(Carry_out));

  // Notes on the sheet:
  //   Carry in
endmodule

module ShiftLeft (
  input  [7:0] X,
  input  [7:0] Y,
  output [7:0] result
);

  Shifter shifter_1 (.in(X), .\dist (Y[2:0]), .out(result));
endmodule

module LogicalRightShift (
  input  [7:0] X,
  input  [7:0] Y,
  output [7:0] result
);

  Shifter #(.shift("lr")) shifter_1 (.in(X), .\dist (Y[2:0]), .out(result));
endmodule

module ArithmeticRightShift (
  input  [7:0] X,
  input  [7:0] Y,
  output [7:0] result
);

  Shifter #(.shift("ar")) shifter_1 (.in(X), .\dist (Y[2:0]), .out(result));
endmodule

module Comparator (
  input  [7:0] X,
  input  [7:0] Y,
  output [7:0] result,
  output eq
);

  Comparator_part comparator_1 (.a(X), .b(Y), .eq(eq), .lt(result[0]));  // open: gt

  assign result[7:1] = {7{1'b0}};
endmodule

module Output_Flag (
  input  [2:0] OP_Code,
  input  [7:0] x,
  input  [7:0] y,
  input  [7:0] Result,
  input  Add_C_out,
  input  Sub_C_out,
  input  EQ_In,
  output SF_Out,
  output ZF_Out,
  output EQ_Out,
  output CF_Out,
  output OF
);

  wire add_signed_overflow_1_add_of_result, comparator_3_eq, comparator_4_eq, signed_overflow_1_sub_of_result;

  Comparator_part #(.width(1)) comparator_1 (.a(Result[7]), .b(1'b1), .eq(SF_Out));  // open: gt, lt
  Comparator_part comparator_2 (.a(Result), .b({8{1'b0}}), .eq(ZF_Out));  // open: gt, lt
  Comparator_part #(.width(1)) comparator_3 (.a(Add_C_out), .b(1'b1), .eq(comparator_3_eq));  // open: gt, lt
  Multiplexer_part #(.select(3), .enable("false")) multiplexer_1 (
    .in0(1'b0), .in1(1'b0), .in2(comparator_3_eq), .in3(comparator_4_eq), .in4(1'b0), .in5(1'b0), .in6(1'b0),
    .in7(1'b0), .out(CF_Out), .sel(OP_Code));
  Comparator_part #(.width(1)) comparator_4 (.a(Sub_C_out), .b(1'b0), .eq(comparator_4_eq));  // open: gt, lt
  Signed_Overflow signed_overflow_1 (
    .x7(x[7]), .in_2(y), .r7(Result[7]), .sub_of_result(signed_overflow_1_sub_of_result));
  add_signed_overflow add_signed_overflow_1 (
    .x7(x[7]), .y7(y[7]), .r7(Result[7]), .add_of_result(add_signed_overflow_1_add_of_result));
  Multiplexer_part #(.select(3), .enable("false")) multiplexer_2 (
    .in0(1'b0), .in1(1'b0), .in2(add_signed_overflow_1_add_of_result), .in3(signed_overflow_1_sub_of_result),
    .in4(1'b0), .in5(1'b0), .in6(1'b0), .in7(1'b0), .out(OF), .sel(OP_Code));

  assign EQ_Out = EQ_In;
endmodule

module Signed_Overflow (
  input  x7,
  input  [7:0] in_2,
  input  r7,
  output sub_of_result
);

  wire and_1_out, and_2_out, and_3_out, and_4_out, not_2_out, not_3_out, not_4_out;
  wire [7:0] adder_1_out, not_1_out;

  assign not_1_out = ~in_2;  // NOT_Gate not_1, 8 bits wide
  Adder_part adder_1 (.a(not_1_out), .b(8'h1), .out(adder_1_out));  // open: cin, cout
  not not_2 (not_2_out, r7);
  and and_1 (and_1_out, x7, adder_1_out[7]);
  and and_2 (and_2_out, and_1_out, not_2_out);
  not not_3 (not_3_out, x7);
  and and_3 (and_3_out, not_3_out, not_4_out);
  not not_4 (not_4_out, adder_1_out[7]);
  and and_4 (and_4_out, and_3_out, r7);
  or or_1 (sub_of_result, and_2_out, and_4_out);
endmodule

module add_signed_overflow (
  input  x7,
  input  y7,
  input  r7,
  output add_of_result
);

  wire and_1_out, and_2_out, and_3_out, and_4_out, not_1_out, not_2_out, not_3_out;

  not not_1 (not_1_out, r7);
  and and_1 (and_1_out, x7, y7);
  and and_2 (and_2_out, and_1_out, not_1_out);
  not not_2 (not_2_out, x7);
  and and_3 (and_3_out, not_2_out, not_3_out);
  not not_3 (not_3_out, y7);
  and and_4 (and_4_out, and_3_out, r7);
  or or_1 (add_of_result, and_2_out, and_4_out);
endmodule
