// Logisim project part1.circ as structural Verilog: 4 circuits, main circuit main
module main (
  input  [3:0] X,
  input  [1:0] Y,
  input  CarryIn,
  output [3:0] Sum,
  output CarryOut
);

  wire [3:0] signext2to4__4_bit_output;

  signext2to4 signext2to4 (._2_bit_input(Y), ._4_bit_output(signext2to4__4_bit_output));
  fulladder4 fulladder4 (
    ._4_bit_x(X), ._4_bit_y(signext2to4__4_bit_output), .carry_in(CarryIn), .sum(Sum), .carry_out(CarryOut));

  // Notes on the sheet:
  //   cs31 lab3, part 1
  //   Caroline Yao, Michael Lu
  //   This is the main circuit.  Please build your sign extender
  //   and adder circuits as sub-circuits, and then test them here.
endmodule

module signext2to4 (
  input  [1:0] _2_bit_input,
  output [3:0] _4_bit_output
);


  assign _4_bit_output = {{3{_2_bit_input[1]}}, _2_bit_input[0]};
endmodule

module fulladder (
  input  C_in,
  input  x,
  input  y,
  output sum,
  output C_out
);

  wire and_1_out, and_2_out, xor_1_out;

  xor xor_1 (xor_1_out, x, y);
  and and_1 (and_1_out, x, y);
  xor xor_2 (sum, xor_1_out, C_in);
  and and_2 (and_2_out, xor_1_out, C_in);
  or or_1 (C_out, and_2_out, and_1_out);
endmodule

module fulladder4 (
  input  [3:0] _4_bit_x,
  input  [3:0] _4_bit_y,
  input  carry_in,
  output [3:0] sum,
  output carry_out
);

  wire fulladder_1_c_out, fulladder_2_c_out, fulladder_3_c_out;

  fulladder fulladder_1 (.x(_4_bit_x[0]), .y(_4_bit_y[0]), .C_in(carry_in), .C_out(fulladder_1_c_out), .sum(sum[0]));
  fulladder fulladder_2 (
    .x(_4_bit_x[1]), .y(_4_bit_y[1]), .C_in(fulladder_1_c_out), .C_out(fulladder_2_c_out), .sum(sum[1]));
  fulladder fulladder_3 (
    .x(_4_bit_x[2]), .y(_4_bit_y[2]), .C_in(fulladder_2_c_out), .C_out(fulladder_3_c_out), .sum(sum[2]));
  fulladder fulladder_4 (.x(_4_bit_x[3]), .y(_4_bit_y[3]), .C_in(fulladder_3_c_out), .C_out(carry_out), .sum(sum[3]));
endmodule
